// Digital circuit risc-v-computer.dig as structural Verilog
module risc_v_computer (
  input  clk,
  output [31:0] out_1,
  output [31:0] out_2,
  output [31:0] out_3,
  output [31:0] _3,
  output [4:0] out_5,
  output [4:0] out_6,
  output [4:0] out_7,
  output [31:0] out_8,
  output [31:0] out_9,
  output [31:0] out_10,
  output [11:0] out_11
);

  wire addrflag_mem, addrflag_peripheral, addrflag_ssd, and_1_out, ard_en, crd_en, Cust_op, jrd_en, lrd_en,
       mret, nor_2_out, not_1_out, Oe_mem, Oe_memop, Oe_ssd, PC_except, PC_inited, PC_jmp, PC_jmpen, rd_en,
       We_mem;
  wire [3:0] storebytes_size;
  wire [4:0] driver_11_out;
  wire [5:0] csr_op;
  wire [6:0] imm_7;
  wire [7:0] mechine_op;
  wire [8:0] jmp_op, mem_op;
  wire [11:0] Addr_csr1;
  wire [18:0] alu_op;
  wire [19:0] imm_20;
  wire [23:0] addr_iop;
  wire [29:24] mem_addr;
  wire [31:0] Addr_except, Addr_jmp, Addr_jmpto, ard_out, crd_out, Data_csr, data_mem, data_memrd,
       Instrction_Reg_q, Invalid_op, jrd_out, lrd_out, Out_csr1, Out_csr2, program_counter_1_pc_next;

  or or_1 (rd_en, jrd_en, ard_en, crd_en, lrd_en);
  or or_2 (PC_jmpen, PC_jmpen, PC_except);
  assign Addr_jmpto = PC_except ? Addr_except : 32'bz;  // Driver driver_1
  not not_1 (not_1_out, PC_inited);
  assign out_3 = not_1_out ? 32'h80000000 : 32'bz;  // Driver driver_2
  assign out_8 = jrd_en ? jrd_out : 32'bz;  // Driver driver_3
  assign out_8 = ard_en ? ard_out : 32'bz;  // Driver driver_4
  assign out_8 = crd_en ? crd_out : 32'bz;  // Driver driver_5
  assign out_8 = lrd_en ? lrd_out : 32'bz;  // Driver driver_6
  program_counter program_counter_1 (
    .En(1'b1), .Clock(clk), .Addr_set(out_3), .Addr_jmp(Addr_jmpto), .En_jmp(PC_jmpen),
    .PC_next(program_counter_1_pc_next));
  and and_1 (and_1_out, PC_jmp, ~PC_except);  // And
  instruction_decoder instruction_decoder_1 (
    .Instruction_In(_3), .EN(1'b1), .mechie_op(mechine_op), .rd(out_5), .rs1(out_6), .rs2(out_7),
    .imm_2531(imm_7), .imm_1231(imm_20), .imm_2032(out_11), .invalid(Invalid_op), .csr_op(csr_op),
    .jmp_op(jmp_op), .alu_op(alu_op), .SL_op(mem_op), .Cust_op(Cust_op));
  assign out_2 = not_1_out ? 32'h80000004 : 32'bz;  // Driver driver_7
  assign Addr_jmpto = and_1_out ? Addr_jmp : 32'bz;  // Driver driver_8
  assign out_2 = PC_inited ? program_counter_1_pc_next : 32'bz;  // Driver driver_9
  mechine_op_unit mechine_op_unit_1 (.mechine_op(mechine_op), .mret(mret));
  Register #(.Bits(32)) Instrction_Reg (.D(out_2), .C(clk), .en(1'b1), .Q(Instrction_Reg_q));
  assign out_3 = PC_inited ? Instrction_Reg_q : 32'bz;  // Driver driver_10
  instuction_jump_unit instuction_jump_unit_1 (
    .jmp_op(jmp_op), .PC_cur(out_3), .PC_next(out_2), .rs1_in(out_9), .rs2_in(out_10), .Imm12_in(out_11),
    .Imm20_in(imm_20), .Imm7_in(imm_7), .offset_5(out_5), .Addr_jmp(Addr_jmp), .rd_out(jrd_out),
    .EN_out(jrd_en), .En_jmp(PC_jmp));
  cust_ctrl cust_ctrl_1 (.op_code(_3), .cust_code(Cust_op), .Clock(clk), .PC_init(PC_inited));
  csr csr_1 (
    .CSRCode_in(csr_op), .Data_in(out_9), .Csr_Addr(out_11), .Imm5_in(out_6), .Clock(clk),
    .Data_temp(Out_csr1), .En(crd_en), .Addr_csr(Addr_csr1), .Out_rd(crd_out), .Out_csr(Data_csr));
  assign driver_11_out = rd_en ? out_5 : 5'bz;  // Driver driver_11
  risc_v_registers risc_v_registers_1 (
    .OE_P1(out_6), .Din(out_8), .Clock(clk), .WE(driver_11_out), .OE_P2(out_7), .OE_P3(5'b00010),
    .Output_P1(out_9), .Output_P2(out_10), .Output_P3(out_1));
  memory memory_1 (
    .Addr({addrflag_peripheral, addrflag_ssd, mem_addr, addr_iop}), .Data_in(data_mem), .WE(We_mem),
    .OE(Oe_mem), .ByteSize_in(storebytes_size), .Clock(clk), .Addr_PC(out_3), .OE_PC(addrflag_mem),
    .Data_out(data_memrd), .DataPC_out(_3));
  boot_rom boot_rom_1 (.Addr(out_3[7:0]), .En(out_3[31]), .Out_code(_3));
  int_except_unit int_except_unit_1 (
    .Data_csr(Data_csr), .WE_CSR(crd_en), .Addr_csrw(Addr_csr1), .Clock(clk), .Addr_csr1(Addr_csr1),
    .Addr_csr2({12{1'b0}}), .Exception_code(Invalid_op), .Interrupt_timer(1'b0), .Interrupt_soft(1'b0),
    .Interrupt_peripheral(1'b0), .PC_Addr(out_3), .PC_ip(_3), .PC_next(out_2), .mret(mret),
    .Out_csr1(Out_csr1), .Out_csr2(Out_csr2), .En_jmp(PC_except), .Addr_jmp(Addr_except));  // open: mip_in, mip_en, mip_out
  nor nor_1 (addrflag_mem, addrflag_peripheral, out_3[31]);
  ROM #(.AddrBits(24), .Bits(8)) Program_Rom (.A(addr_iop), .sel(Oe_ssd), .D(data_memrd[7:0]));
  PullDown #(.Bits(32)) pulldown_1 (.out(data_memrd));
  alu alu_1 (
    .Alu_in(alu_op), .rs1_in(out_9), .rs2_in(out_10), .Imm12_in(out_11), .Clock(clk), .rd_out(ard_out),
    .EN_out(ard_en), .InvlidOP_out(Invalid_op));
  memory_operation_unit memory_operation_unit_1 (
    .MemOp_in(mem_op), .Data_in(data_memrd), .rs1(out_9), .rs2(out_10), .Offset_12(out_11), .Offset_7(imm_7),
    .Offset_5(out_5), .imm_20(imm_20), .we_out(We_mem),
    .Addr_out({addrflag_peripheral, addrflag_ssd, mem_addr, addr_iop}), .Mem_out(data_mem),
    .StoreByteSize_out(storebytes_size), .oe_out(Oe_memop), .RegWE_out(lrd_en), .rd_out(lrd_out));
  nor nor_2 (nor_2_out, addrflag_peripheral, addrflag_ssd);
  and and_2 (Oe_ssd, addrflag_ssd, Oe_memop);
  and and_3 (Oe_mem, nor_2_out, Oe_memop);
  // also tied to GND on the sheet: {data_memrd[8], data_memrd[9], data_memrd[10], data_memrd[11], data_memrd[12], data_memrd[13], data_memrd[14], data_memrd[15], data_memrd[16], data_memrd[17], data_memrd[18], data_memrd[19], data_memrd[20], data_memrd[21], data_memrd[22], data_memrd[23], data_memrd[24], data_memrd[25], data_memrd[26], data_memrd[27], data_memrd[28], data_memrd[29], data_memrd[30], data_memrd[31]}

  // Other names for the same wires on the sheet: _2out[31:0] = out_1; Addr_csrw[11:0] = Addr_csr1; c = clk;
  //   WE_CSR = crd_en; imm_12[11:0] = out_11; instruction_code[31:0] = _3;
  //   mem_addr (some bits) = {addrflag_peripheral, addrflag_ssd, addr_iop}; addr_real[23:0] = out_3[23:0];
  //   PC_exec[31:0] = out_3; addrflag_boot = out_3[31]; PC_next[31:0] = out_2; rd[4:0] = out_5; rd_out[31:0] = out_8;
  //   rs1[4:0] = out_6; rs1_data[31:0] = out_9; rs2[4:0] = out_7; rs2_data[31:0] = out_10

  // Notes on the sheet:
  //   Reg-Write-Bus
  //   Instruction Program Counter Bus
  //   contents of Program_Rom (hex, n*v repeats v):
  //   6*16
  //   Memory Bus
endmodule
